// Logisim project ENIGMA.circ as structural Verilog
module LATCH_D (
  input  D,
  input  CLK,
  output Q
);

  wire and_1_out, and_2_out, nor_1_out;

  and and_1 (and_1_out, D, CLK);
  and and_2 (and_2_out, CLK, ~D);  // AND_Gate
  nor nor_1 (nor_1_out, and_1_out, Q);
  nor nor_2 (Q, nor_1_out, and_2_out);
endmodule

module NEXTINDEX_RITORNO (
  input  [4:0] INPUT_INDICE,
  input  [4:0] INPUT_ROTORE,
  output [4:0] SHIFT_INDICE
);

  wire comparator_1_lt;
  wire [4:0] subtractor_1_out, subtractor_2_out;

  Subtractor #(.width(5)) subtractor_1 (.a(INPUT_INDICE), .b(INPUT_ROTORE), .out(subtractor_1_out));  // open: bin, bout
  Comparator #(.width(5), .mode("unsigned")) comparator_1 (
    .a(INPUT_INDICE), .b(INPUT_ROTORE), .lt(comparator_1_lt));  // open: gt, eq
  Subtractor #(.width(5)) subtractor_2 (.a(subtractor_1_out), .b(5'b00110), .out(subtractor_2_out));  // open: bin, bout
  Multiplexer #(.width(5), .enable("false")) multiplexer_1 (
    .in0(subtractor_1_out), .in1(subtractor_2_out), .out(SHIFT_INDICE), .sel(comparator_1_lt));
endmodule

module ROTOREA (
  input  INPUT_1,
  input  [25:0] INPUT_26_LETTERE,
  input  [4:0] POSIZIONE_ROTORE,
  input  [25:0] INPUT_26_LETTERE_2,
  output OUTPUT_1,
  output [25:0] OUTPUT_26_LETTERE,
  output [25:0] OUTPUT_26_LETTERE_2
);

  wire demultiplexer_1_out26, demultiplexer_2_out26, demultiplexer_3_out26, demultiplexer_4_out26;
  wire [4:0] bitfinder_1_index, bitfinder_2_index, bitfinder_3_index, bitfinder_4_index,
       nextindex_andata_1_shift_indice, nextindex_andata_2_shift_indice, nextindex_ritorno_1_shift_indice,
       nextindex_ritorno_2_shift_indice;
  wire [25:0] demultiplexer_3_out0, demultiplexer_4_out5;

  Demultiplexer #(.select(5), .enable("false")) demultiplexer_1 (
    .out0(OUTPUT_26_LETTERE[0]), .out1(OUTPUT_26_LETTERE[1]), .out2(OUTPUT_26_LETTERE[2]),
    .out3(OUTPUT_26_LETTERE[3]), .out4(OUTPUT_26_LETTERE[4]), .out5(OUTPUT_26_LETTERE[5]),
    .out6(OUTPUT_26_LETTERE[6]), .out7(OUTPUT_26_LETTERE[7]), .out8(OUTPUT_26_LETTERE[8]),
    .out9(OUTPUT_26_LETTERE[9]), .out10(OUTPUT_26_LETTERE[10]), .out11(OUTPUT_26_LETTERE[11]),
    .out12(OUTPUT_26_LETTERE[12]), .out13(OUTPUT_26_LETTERE[13]), .out14(OUTPUT_26_LETTERE[14]),
    .out15(OUTPUT_26_LETTERE[15]), .out16(OUTPUT_26_LETTERE[16]), .out17(OUTPUT_26_LETTERE[17]),
    .out18(OUTPUT_26_LETTERE[18]), .out19(OUTPUT_26_LETTERE[19]), .out20(OUTPUT_26_LETTERE[20]),
    .out21(OUTPUT_26_LETTERE[21]), .out22(OUTPUT_26_LETTERE[22]), .out23(OUTPUT_26_LETTERE[23]),
    .out24(OUTPUT_26_LETTERE[24]), .out25(OUTPUT_26_LETTERE[25]), .out26(demultiplexer_1_out26),
    .out27(demultiplexer_1_out26), .out28(demultiplexer_1_out26), .out29(demultiplexer_1_out26),
    .out30(demultiplexer_1_out26), .out31(demultiplexer_1_out26), .in(INPUT_1),
    .sel(nextindex_andata_1_shift_indice));
  Demultiplexer #(.select(5), .enable("false")) demultiplexer_2 (
    .out0(OUTPUT_26_LETTERE_2[0]), .out1(OUTPUT_26_LETTERE_2[1]), .out2(OUTPUT_26_LETTERE_2[2]),
    .out3(OUTPUT_26_LETTERE_2[3]), .out4(OUTPUT_26_LETTERE_2[4]), .out5(OUTPUT_26_LETTERE_2[5]),
    .out6(OUTPUT_26_LETTERE_2[6]), .out7(OUTPUT_26_LETTERE_2[7]), .out8(OUTPUT_26_LETTERE_2[8]),
    .out9(OUTPUT_26_LETTERE_2[9]), .out10(OUTPUT_26_LETTERE_2[10]), .out11(OUTPUT_26_LETTERE_2[11]),
    .out12(OUTPUT_26_LETTERE_2[12]), .out13(OUTPUT_26_LETTERE_2[13]), .out14(OUTPUT_26_LETTERE_2[14]),
    .out15(OUTPUT_26_LETTERE_2[15]), .out16(OUTPUT_26_LETTERE_2[16]), .out17(OUTPUT_26_LETTERE_2[17]),
    .out18(OUTPUT_26_LETTERE_2[18]), .out19(OUTPUT_26_LETTERE_2[19]), .out20(OUTPUT_26_LETTERE_2[20]),
    .out21(OUTPUT_26_LETTERE_2[21]), .out22(OUTPUT_26_LETTERE_2[22]), .out23(OUTPUT_26_LETTERE_2[23]),
    .out24(OUTPUT_26_LETTERE_2[24]), .out25(OUTPUT_26_LETTERE_2[25]), .out26(demultiplexer_2_out26),
    .out27(demultiplexer_2_out26), .out28(demultiplexer_2_out26), .out29(demultiplexer_2_out26),
    .out30(demultiplexer_2_out26), .out31(demultiplexer_2_out26), .in(INPUT_1),
    .sel(nextindex_ritorno_1_shift_indice));
  BitFinder #(.width(26)) bitfinder_1 (.in(demultiplexer_3_out0), .index(bitfinder_1_index));  // open: found
  NEXTINDEX_ANDATA nextindex_andata_1 (
    .INPUT_ROTORE(POSIZIONE_ROTORE), .SHIFT_INDICE(nextindex_andata_1_shift_indice),
    .INPUT_INDICE(bitfinder_1_index));
  BitFinder #(.width(26)) bitfinder_2 (.in(demultiplexer_4_out5), .index(bitfinder_2_index));  // open: found
  NEXTINDEX_RITORNO nextindex_ritorno_1 (
    .INPUT_INDICE(bitfinder_2_index), .INPUT_ROTORE(POSIZIONE_ROTORE),
    .SHIFT_INDICE(nextindex_ritorno_1_shift_indice));
  Demultiplexer #(.select(5), .enable("false")) demultiplexer_3 (
    .out0(demultiplexer_3_out0[5]), .out1(demultiplexer_3_out0[9]), .out2(demultiplexer_3_out0[24]),
    .out3(demultiplexer_3_out0[15]), .out4(demultiplexer_3_out0[7]), .out5(demultiplexer_3_out0[0]),
    .out6(demultiplexer_3_out0[21]), .out7(demultiplexer_3_out0[25]), .out8(demultiplexer_3_out0[18]),
    .out9(demultiplexer_3_out0[10]), .out10(demultiplexer_3_out0[16]), .out11(demultiplexer_3_out0[2]),
    .out12(demultiplexer_3_out0[23]), .out13(demultiplexer_3_out0[4]), .out14(demultiplexer_3_out0[11]),
    .out15(demultiplexer_3_out0[8]), .out16(demultiplexer_3_out0[20]), .out17(demultiplexer_3_out0[13]),
    .out18(demultiplexer_3_out0[3]), .out19(demultiplexer_3_out0[22]), .out20(demultiplexer_3_out0[12]),
    .out21(demultiplexer_3_out0[1]), .out22(demultiplexer_3_out0[14]), .out23(demultiplexer_3_out0[17]),
    .out24(demultiplexer_3_out0[19]), .out25(demultiplexer_3_out0[6]), .out26(demultiplexer_3_out26),
    .out27(demultiplexer_3_out26), .out28(demultiplexer_3_out26), .out29(demultiplexer_3_out26),
    .out31(demultiplexer_3_out26), .in(INPUT_1), .sel(nextindex_andata_2_shift_indice));  // open: out30
  Demultiplexer #(.select(5), .enable("false")) demultiplexer_4 (
    .out0(demultiplexer_4_out5[5]), .out1(demultiplexer_4_out5[21]), .out2(demultiplexer_4_out5[11]),
    .out3(demultiplexer_4_out5[18]), .out4(demultiplexer_4_out5[13]), .out5(demultiplexer_4_out5[0]),
    .out6(demultiplexer_4_out5[25]), .out7(demultiplexer_4_out5[4]), .out8(demultiplexer_4_out5[15]),
    .out9(demultiplexer_4_out5[1]), .out10(demultiplexer_4_out5[9]), .out11(demultiplexer_4_out5[14]),
    .out12(demultiplexer_4_out5[20]), .out13(demultiplexer_4_out5[17]), .out14(demultiplexer_4_out5[22]),
    .out15(demultiplexer_4_out5[3]), .out16(demultiplexer_4_out5[10]), .out17(demultiplexer_4_out5[23]),
    .out18(demultiplexer_4_out5[8]), .out19(demultiplexer_4_out5[24]), .out20(demultiplexer_4_out5[16]),
    .out21(demultiplexer_4_out5[6]), .out22(demultiplexer_4_out5[19]), .out23(demultiplexer_4_out5[12]),
    .out24(demultiplexer_4_out5[2]), .out25(demultiplexer_4_out5[7]), .out26(demultiplexer_4_out26),
    .out27(demultiplexer_4_out26), .out28(demultiplexer_4_out26), .out29(demultiplexer_4_out26),
    .out30(demultiplexer_4_out26), .out31(demultiplexer_4_out26), .in(INPUT_1),
    .sel(nextindex_ritorno_2_shift_indice));
  BitFinder #(.width(26)) bitfinder_3 (.in(INPUT_26_LETTERE), .index(bitfinder_3_index));  // open: found
  BitFinder #(.width(26)) bitfinder_4 (.in(INPUT_26_LETTERE_2), .index(bitfinder_4_index));  // open: found
  NEXTINDEX_ANDATA nextindex_andata_2 (
    .INPUT_ROTORE(POSIZIONE_ROTORE), .SHIFT_INDICE(nextindex_andata_2_shift_indice),
    .INPUT_INDICE(bitfinder_3_index));
  NEXTINDEX_RITORNO nextindex_ritorno_2 (
    .INPUT_INDICE(bitfinder_4_index), .INPUT_ROTORE(POSIZIONE_ROTORE),
    .SHIFT_INDICE(nextindex_ritorno_2_shift_indice));

  assign OUTPUT_1 = INPUT_1;

  // Other names for the same wires on the sheet: ROTORE[4:0] = POSIZIONE_ROTORE

  // Notes on the sheet:
  //   ANDATA
  //   RITORNO
  //   ROTORE A
endmodule

module ROTOREB (
  input  INPUT_1,
  input  [25:0] INPUT_26_LETTERE,
  input  [4:0] POSIZIONE_ROTORE,
  input  [25:0] INPUT_26_LETTERE_2,
  output OUTPUT_1,
  output [25:0] OUTPUT_26_LETTERE,
  output [25:0] OUTPUT_26_LETTERE_2
);

  wire demultiplexer_1_out26, demultiplexer_2_out26, demultiplexer_3_out26, demultiplexer_4_out26;
  wire [4:0] bitfinder_1_index, bitfinder_2_index, bitfinder_3_index, bitfinder_4_index,
       nextindex_andata_1_shift_indice, nextindex_andata_2_shift_indice, nextindex_ritorno_1_shift_indice,
       nextindex_ritorno_2_shift_indice;
  wire [25:0] demultiplexer_3_out8, demultiplexer_4_out12;

  Demultiplexer #(.select(5), .enable("false")) demultiplexer_1 (
    .out0(OUTPUT_26_LETTERE[0]), .out1(OUTPUT_26_LETTERE[1]), .out2(OUTPUT_26_LETTERE[2]),
    .out3(OUTPUT_26_LETTERE[3]), .out4(OUTPUT_26_LETTERE[4]), .out5(OUTPUT_26_LETTERE[5]),
    .out6(OUTPUT_26_LETTERE[6]), .out7(OUTPUT_26_LETTERE[7]), .out8(OUTPUT_26_LETTERE[8]),
    .out9(OUTPUT_26_LETTERE[9]), .out10(OUTPUT_26_LETTERE[10]), .out11(OUTPUT_26_LETTERE[11]),
    .out12(OUTPUT_26_LETTERE[12]), .out13(OUTPUT_26_LETTERE[13]), .out14(OUTPUT_26_LETTERE[14]),
    .out15(OUTPUT_26_LETTERE[15]), .out16(OUTPUT_26_LETTERE[16]), .out17(OUTPUT_26_LETTERE[17]),
    .out18(OUTPUT_26_LETTERE[18]), .out19(OUTPUT_26_LETTERE[19]), .out20(OUTPUT_26_LETTERE[20]),
    .out21(OUTPUT_26_LETTERE[21]), .out22(OUTPUT_26_LETTERE[22]), .out23(OUTPUT_26_LETTERE[23]),
    .out24(OUTPUT_26_LETTERE[24]), .out25(OUTPUT_26_LETTERE[25]), .out26(demultiplexer_1_out26),
    .out27(demultiplexer_1_out26), .out28(demultiplexer_1_out26), .out29(demultiplexer_1_out26),
    .out30(demultiplexer_1_out26), .out31(demultiplexer_1_out26), .in(INPUT_1),
    .sel(nextindex_andata_1_shift_indice));
  Demultiplexer #(.select(5), .enable("false")) demultiplexer_2 (
    .out0(OUTPUT_26_LETTERE_2[0]), .out1(OUTPUT_26_LETTERE_2[1]), .out2(OUTPUT_26_LETTERE_2[2]),
    .out3(OUTPUT_26_LETTERE_2[3]), .out4(OUTPUT_26_LETTERE_2[4]), .out5(OUTPUT_26_LETTERE_2[5]),
    .out6(OUTPUT_26_LETTERE_2[6]), .out7(OUTPUT_26_LETTERE_2[7]), .out8(OUTPUT_26_LETTERE_2[8]),
    .out9(OUTPUT_26_LETTERE_2[9]), .out10(OUTPUT_26_LETTERE_2[10]), .out11(OUTPUT_26_LETTERE_2[11]),
    .out12(OUTPUT_26_LETTERE_2[12]), .out13(OUTPUT_26_LETTERE_2[13]), .out14(OUTPUT_26_LETTERE_2[14]),
    .out15(OUTPUT_26_LETTERE_2[15]), .out16(OUTPUT_26_LETTERE_2[16]), .out17(OUTPUT_26_LETTERE_2[17]),
    .out18(OUTPUT_26_LETTERE_2[18]), .out19(OUTPUT_26_LETTERE_2[19]), .out20(OUTPUT_26_LETTERE_2[20]),
    .out21(OUTPUT_26_LETTERE_2[21]), .out22(OUTPUT_26_LETTERE_2[22]), .out23(OUTPUT_26_LETTERE_2[23]),
    .out24(OUTPUT_26_LETTERE_2[24]), .out25(OUTPUT_26_LETTERE_2[25]), .out26(demultiplexer_2_out26),
    .out27(demultiplexer_2_out26), .out28(demultiplexer_2_out26), .out29(demultiplexer_2_out26),
    .out30(demultiplexer_2_out26), .out31(demultiplexer_2_out26), .in(INPUT_1),
    .sel(nextindex_ritorno_1_shift_indice));
  BitFinder #(.width(26)) bitfinder_1 (.in(demultiplexer_3_out8), .index(bitfinder_1_index));  // open: found
  NEXTINDEX_ANDATA nextindex_andata_1 (
    .INPUT_ROTORE(POSIZIONE_ROTORE), .SHIFT_INDICE(nextindex_andata_1_shift_indice),
    .INPUT_INDICE(bitfinder_1_index));
  BitFinder #(.width(26)) bitfinder_2 (.in(demultiplexer_4_out12), .index(bitfinder_2_index));  // open: found
  NEXTINDEX_RITORNO nextindex_ritorno_1 (
    .INPUT_INDICE(bitfinder_2_index), .INPUT_ROTORE(POSIZIONE_ROTORE),
    .SHIFT_INDICE(nextindex_ritorno_1_shift_indice));
  Demultiplexer #(.select(5), .enable("false")) demultiplexer_3 (
    .out0(demultiplexer_3_out8[12]), .out1(demultiplexer_3_out8[4]), .out2(demultiplexer_3_out8[7]),
    .out3(demultiplexer_3_out8[25]), .out4(demultiplexer_3_out8[16]), .out5(demultiplexer_3_out8[10]),
    .out6(demultiplexer_3_out8[23]), .out7(demultiplexer_3_out8[14]), .out8(demultiplexer_3_out8[0]),
    .out9(demultiplexer_3_out8[6]), .out10(demultiplexer_3_out8[13]), .out11(demultiplexer_3_out8[3]),
    .out12(demultiplexer_3_out8[1]), .out13(demultiplexer_3_out8[24]), .out14(demultiplexer_3_out8[18]),
    .out15(demultiplexer_3_out8[21]), .out16(demultiplexer_3_out8[20]), .out17(demultiplexer_3_out8[2]),
    .out18(demultiplexer_3_out8[19]), .out19(demultiplexer_3_out8[5]), .out20(demultiplexer_3_out8[22]),
    .out21(demultiplexer_3_out8[17]), .out22(demultiplexer_3_out8[8]), .out23(demultiplexer_3_out8[15]),
    .out24(demultiplexer_3_out8[9]), .out25(demultiplexer_3_out8[11]), .out26(demultiplexer_3_out26),
    .out27(demultiplexer_3_out26), .out28(demultiplexer_3_out26), .out29(demultiplexer_3_out26),
    .out30(demultiplexer_3_out26), .out31(demultiplexer_3_out26), .in(INPUT_1),
    .sel(nextindex_andata_2_shift_indice));
  Demultiplexer #(.select(5), .enable("false")) demultiplexer_4 (
    .out0(demultiplexer_4_out12[8]), .out1(demultiplexer_4_out12[12]), .out2(demultiplexer_4_out12[17]),
    .out3(demultiplexer_4_out12[11]), .out4(demultiplexer_4_out12[1]), .out5(demultiplexer_4_out12[19]),
    .out6(demultiplexer_4_out12[9]), .out7(demultiplexer_4_out12[2]), .out8(demultiplexer_4_out12[22]),
    .out9(demultiplexer_4_out12[24]), .out10(demultiplexer_4_out12[5]), .out11(demultiplexer_4_out12[25]),
    .out12(demultiplexer_4_out12[0]), .out13(demultiplexer_4_out12[10]), .out14(demultiplexer_4_out12[7]),
    .out15(demultiplexer_4_out12[23]), .out16(demultiplexer_4_out12[4]), .out17(demultiplexer_4_out12[21]),
    .out18(demultiplexer_4_out12[14]), .out19(demultiplexer_4_out12[18]), .out20(demultiplexer_4_out12[16]),
    .out21(demultiplexer_4_out12[15]), .out22(demultiplexer_4_out12[20]), .out23(demultiplexer_4_out12[6]),
    .out24(demultiplexer_4_out12[13]), .out25(demultiplexer_4_out12[3]), .out26(demultiplexer_4_out26),
    .out27(demultiplexer_4_out26), .out28(demultiplexer_4_out26), .out29(demultiplexer_4_out26),
    .out30(demultiplexer_4_out26), .out31(demultiplexer_4_out26), .in(INPUT_1),
    .sel(nextindex_ritorno_2_shift_indice));
  NEXTINDEX_ANDATA nextindex_andata_2 (
    .INPUT_ROTORE(POSIZIONE_ROTORE), .SHIFT_INDICE(nextindex_andata_2_shift_indice),
    .INPUT_INDICE(bitfinder_3_index));
  BitFinder #(.width(26)) bitfinder_3 (.in(INPUT_26_LETTERE), .index(bitfinder_3_index));  // open: found
  BitFinder #(.width(26)) bitfinder_4 (.in(INPUT_26_LETTERE_2), .index(bitfinder_4_index));  // open: found
  NEXTINDEX_RITORNO nextindex_ritorno_2 (
    .INPUT_INDICE(bitfinder_4_index), .INPUT_ROTORE(POSIZIONE_ROTORE),
    .SHIFT_INDICE(nextindex_ritorno_2_shift_indice));

  assign OUTPUT_1 = INPUT_1;

  // Other names for the same wires on the sheet: ROTORE[4:0] = POSIZIONE_ROTORE

  // Notes on the sheet:
  //   ANDATA
  //   RITORNO
  //   ROTORE B
endmodule

module ROTOREC (
  input  INPUT_1,
  input  [25:0] INPUT_26_LETTERE,
  input  [4:0] in_3,
  input  [25:0] INPUT_26_LETTERE_2,
  output OUTPUT_1,
  output [25:0] OUTPUT_26_LETTERE,
  output [25:0] OUTPUT_26_LETTERE_2
);

  wire demultiplexer_1_out26, demultiplexer_2_out26, demultiplexer_3_out26, demultiplexer_4_out26;
  wire [4:0] bitfinder_1_index, bitfinder_2_index, bitfinder_3_index, bitfinder_4_index,
       nextindex_andata_1_shift_indice, nextindex_andata_2_shift_indice, nextindex_ritorno_1_shift_indice,
       nextindex_ritorno_2_shift_indice;
  wire [25:0] demultiplexer_3_out0, demultiplexer_4_out23;

  Demultiplexer #(.select(5), .enable("false")) demultiplexer_1 (
    .out0(OUTPUT_26_LETTERE[0]), .out1(OUTPUT_26_LETTERE[1]), .out2(OUTPUT_26_LETTERE[2]),
    .out3(OUTPUT_26_LETTERE[3]), .out4(OUTPUT_26_LETTERE[4]), .out5(OUTPUT_26_LETTERE[5]),
    .out6(OUTPUT_26_LETTERE[6]), .out7(OUTPUT_26_LETTERE[7]), .out8(OUTPUT_26_LETTERE[8]),
    .out9(OUTPUT_26_LETTERE[9]), .out10(OUTPUT_26_LETTERE[10]), .out11(OUTPUT_26_LETTERE[11]),
    .out12(OUTPUT_26_LETTERE[12]), .out13(OUTPUT_26_LETTERE[13]), .out14(OUTPUT_26_LETTERE[14]),
    .out15(OUTPUT_26_LETTERE[15]), .out16(OUTPUT_26_LETTERE[16]), .out17(OUTPUT_26_LETTERE[17]),
    .out18(OUTPUT_26_LETTERE[18]), .out19(OUTPUT_26_LETTERE[19]), .out20(OUTPUT_26_LETTERE[20]),
    .out21(OUTPUT_26_LETTERE[21]), .out22(OUTPUT_26_LETTERE[22]), .out23(OUTPUT_26_LETTERE[23]),
    .out24(OUTPUT_26_LETTERE[24]), .out25(OUTPUT_26_LETTERE[25]), .out26(demultiplexer_1_out26),
    .out27(demultiplexer_1_out26), .out28(demultiplexer_1_out26), .out29(demultiplexer_1_out26),
    .out30(demultiplexer_1_out26), .out31(demultiplexer_1_out26), .in(INPUT_1),
    .sel(nextindex_andata_1_shift_indice));
  Demultiplexer #(.select(5), .enable("false")) demultiplexer_2 (
    .out0(OUTPUT_26_LETTERE_2[0]), .out1(OUTPUT_26_LETTERE_2[1]), .out2(OUTPUT_26_LETTERE_2[2]),
    .out3(OUTPUT_26_LETTERE_2[3]), .out4(OUTPUT_26_LETTERE_2[4]), .out5(OUTPUT_26_LETTERE_2[5]),
    .out6(OUTPUT_26_LETTERE_2[6]), .out7(OUTPUT_26_LETTERE_2[7]), .out8(OUTPUT_26_LETTERE_2[8]),
    .out9(OUTPUT_26_LETTERE_2[9]), .out10(OUTPUT_26_LETTERE_2[10]), .out11(OUTPUT_26_LETTERE_2[11]),
    .out12(OUTPUT_26_LETTERE_2[12]), .out13(OUTPUT_26_LETTERE_2[13]), .out14(OUTPUT_26_LETTERE_2[14]),
    .out15(OUTPUT_26_LETTERE_2[15]), .out16(OUTPUT_26_LETTERE_2[16]), .out17(OUTPUT_26_LETTERE_2[17]),
    .out18(OUTPUT_26_LETTERE_2[18]), .out19(OUTPUT_26_LETTERE_2[19]), .out20(OUTPUT_26_LETTERE_2[20]),
    .out21(OUTPUT_26_LETTERE_2[21]), .out22(OUTPUT_26_LETTERE_2[22]), .out23(OUTPUT_26_LETTERE_2[23]),
    .out24(OUTPUT_26_LETTERE_2[24]), .out25(OUTPUT_26_LETTERE_2[25]), .out26(demultiplexer_2_out26),
    .out27(demultiplexer_2_out26), .out28(demultiplexer_2_out26), .out29(demultiplexer_2_out26),
    .out30(demultiplexer_2_out26), .out31(demultiplexer_2_out26), .in(INPUT_1),
    .sel(nextindex_ritorno_1_shift_indice));
  NEXTINDEX_ANDATA nextindex_andata_1 (
    .INPUT_ROTORE(in_3), .SHIFT_INDICE(nextindex_andata_1_shift_indice), .INPUT_INDICE(bitfinder_1_index));
  BitFinder #(.width(26)) bitfinder_1 (.in(demultiplexer_3_out0), .index(bitfinder_1_index));  // open: found
  BitFinder #(.width(26)) bitfinder_2 (.in(demultiplexer_4_out23), .index(bitfinder_2_index));  // open: found
  NEXTINDEX_RITORNO nextindex_ritorno_1 (
    .INPUT_INDICE(bitfinder_2_index), .INPUT_ROTORE(in_3), .SHIFT_INDICE(nextindex_ritorno_1_shift_indice));
  Demultiplexer #(.select(5), .enable("false")) demultiplexer_3 (
    .out0(demultiplexer_3_out0[23]), .out1(demultiplexer_3_out0[5]), .out2(demultiplexer_3_out0[9]),
    .out3(demultiplexer_3_out0[8]), .out4(demultiplexer_3_out0[4]), .out5(demultiplexer_3_out0[15]),
    .out6(demultiplexer_3_out0[6]), .out7(demultiplexer_3_out0[14]), .out8(demultiplexer_3_out0[7]),
    .out9(demultiplexer_3_out0[24]), .out10(demultiplexer_3_out0[0]), .out11(demultiplexer_3_out0[3]),
    .out12(demultiplexer_3_out0[10]), .out13(demultiplexer_3_out0[18]), .out14(demultiplexer_3_out0[20]),
    .out15(demultiplexer_3_out0[12]), .out16(demultiplexer_3_out0[25]), .out17(demultiplexer_3_out0[2]),
    .out18(demultiplexer_3_out0[21]), .out19(demultiplexer_3_out0[17]), .out20(demultiplexer_3_out0[1]),
    .out21(demultiplexer_3_out0[22]), .out22(demultiplexer_3_out0[11]), .out23(demultiplexer_3_out0[13]),
    .out24(demultiplexer_3_out0[19]), .out25(demultiplexer_3_out0[16]), .out26(demultiplexer_3_out26),
    .out27(demultiplexer_3_out26), .out28(demultiplexer_3_out26), .out29(demultiplexer_3_out26),
    .out30(demultiplexer_3_out26), .out31(demultiplexer_3_out26), .in(INPUT_1),
    .sel(nextindex_andata_2_shift_indice));
  Demultiplexer #(.select(5), .enable("false")) demultiplexer_4 (
    .out0(demultiplexer_4_out23[10]), .out1(demultiplexer_4_out23[20]), .out2(demultiplexer_4_out23[17]),
    .out3(demultiplexer_4_out23[11]), .out4(demultiplexer_4_out23[4]), .out5(demultiplexer_4_out23[1]),
    .out6(demultiplexer_4_out23[6]), .out7(demultiplexer_4_out23[8]), .out8(demultiplexer_4_out23[3]),
    .out9(demultiplexer_4_out23[2]), .out10(demultiplexer_4_out23[12]), .out11(demultiplexer_4_out23[22]),
    .out12(demultiplexer_4_out23[15]), .out13(demultiplexer_4_out23[23]), .out14(demultiplexer_4_out23[7]),
    .out15(demultiplexer_4_out23[5]), .out16(demultiplexer_4_out23[25]), .out17(demultiplexer_4_out23[19]),
    .out18(demultiplexer_4_out23[13]), .out19(demultiplexer_4_out23[24]), .out20(demultiplexer_4_out23[14]),
    .out21(demultiplexer_4_out23[18]), .out22(demultiplexer_4_out23[21]), .out23(demultiplexer_4_out23[0]),
    .out24(demultiplexer_4_out23[9]), .out25(demultiplexer_4_out23[16]), .out26(demultiplexer_4_out26),
    .out27(demultiplexer_4_out26), .out28(demultiplexer_4_out26), .out29(demultiplexer_4_out26),
    .out30(demultiplexer_4_out26), .out31(demultiplexer_4_out26), .in(INPUT_1),
    .sel(nextindex_ritorno_2_shift_indice));
  BitFinder #(.width(26)) bitfinder_3 (.in(INPUT_26_LETTERE), .index(bitfinder_3_index));  // open: found
  BitFinder #(.width(26)) bitfinder_4 (.in(INPUT_26_LETTERE_2), .index(bitfinder_4_index));  // open: found
  NEXTINDEX_ANDATA nextindex_andata_2 (
    .INPUT_ROTORE(in_3), .SHIFT_INDICE(nextindex_andata_2_shift_indice), .INPUT_INDICE(bitfinder_3_index));
  NEXTINDEX_RITORNO nextindex_ritorno_2 (
    .INPUT_INDICE(bitfinder_4_index), .INPUT_ROTORE(in_3), .SHIFT_INDICE(nextindex_ritorno_2_shift_indice));

  assign OUTPUT_1 = INPUT_1;

  // Other names for the same wires on the sheet: ROTORE[4:0] = in_3

  // Notes on the sheet:
  //   ANDATA
  //   RITORNO
  //   INPUT 
  //   ROTORE
  //   ROTORE C
endmodule

module RIFLETTORE (
  input  INPUT_1,
  input  [25:0] INPUT_26_LETTERE,
  output [25:0] OUTPUT_26_LETTERE
);

  wire demultiplexer_1_out26;
  wire [4:0] bitfinder_1_index;

  Demultiplexer #(.select(5), .enable("false")) demultiplexer_1 (
    .out0(OUTPUT_26_LETTERE[12]), .out1(OUTPUT_26_LETTERE[22]), .out2(OUTPUT_26_LETTERE[24]),
    .out3(OUTPUT_26_LETTERE[5]), .out4(OUTPUT_26_LETTERE[18]), .out5(OUTPUT_26_LETTERE[3]),
    .out6(OUTPUT_26_LETTERE[25]), .out7(OUTPUT_26_LETTERE[16]), .out8(OUTPUT_26_LETTERE[14]),
    .out9(OUTPUT_26_LETTERE[21]), .out10(OUTPUT_26_LETTERE[15]), .out11(OUTPUT_26_LETTERE[19]),
    .out12(OUTPUT_26_LETTERE[0]), .out13(OUTPUT_26_LETTERE[23]), .out14(OUTPUT_26_LETTERE[8]),
    .out15(OUTPUT_26_LETTERE[10]), .out16(OUTPUT_26_LETTERE[7]), .out17(OUTPUT_26_LETTERE[20]),
    .out18(OUTPUT_26_LETTERE[4]), .out19(OUTPUT_26_LETTERE[11]), .out20(OUTPUT_26_LETTERE[17]),
    .out21(OUTPUT_26_LETTERE[9]), .out22(OUTPUT_26_LETTERE[1]), .out23(OUTPUT_26_LETTERE[13]),
    .out24(OUTPUT_26_LETTERE[2]), .out25(OUTPUT_26_LETTERE[6]), .out26(demultiplexer_1_out26),
    .out27(demultiplexer_1_out26), .out28(demultiplexer_1_out26), .out29(demultiplexer_1_out26),
    .out30(demultiplexer_1_out26), .out31(demultiplexer_1_out26), .in(INPUT_1), .sel(bitfinder_1_index));
  BitFinder #(.width(26)) bitfinder_1 (.in(INPUT_26_LETTERE), .index(bitfinder_1_index));  // open: found

  // Notes on the sheet:
  //   RIFLETTORE
endmodule

module NEXTINDEX_ANDATA (
  input  [4:0] INPUT_INDICE,
  input  [4:0] INPUT_ROTORE,
  output [4:0] SHIFT_INDICE
);

  wire comparator_1_gt;
  wire [5:0] adder_1_out, bit_extender_1_out, bit_extender_2_out, subtractor_1_out;
  wire [5:5] multiplexer_1_out;

  assign bit_extender_1_out = {{1{1'b0}}, INPUT_INDICE};  // Bit_Extender bit_extender_1
  assign bit_extender_2_out = {{1{1'b0}}, INPUT_ROTORE};  // Bit_Extender bit_extender_2
  Adder #(.width(6)) adder_1 (.a(bit_extender_1_out), .b(bit_extender_2_out), .out(adder_1_out));  // open: cin, cout
  Comparator #(.width(6), .mode("unsigned")) comparator_1 (
    .a(adder_1_out), .b(6'b011001), .gt(comparator_1_gt));  // open: eq, lt
  Subtractor #(.width(6)) subtractor_1 (.a(adder_1_out), .b(6'b011010), .out(subtractor_1_out));  // open: bin, bout
  Multiplexer #(.width(6), .enable("false")) multiplexer_1 (
    .in0(adder_1_out), .in1(subtractor_1_out), .out({multiplexer_1_out[5], SHIFT_INDICE}),
    .sel(comparator_1_gt));
endmodule

module ENIGMA (
  input  A,
  input  B,
  input  C,
  input  [4:0] in_4,
  input  [4:0] in_5,
  input  [4:0] in_6,
  input  D,
  input  E,
  input  F,
  input  G,
  input  H,
  input  I,
  input  J,
  input  K,
  input  L,
  input  M,
  input  N,
  input  O,
  input  P,
  input  Q,
  input  R,
  input  S,
  input  S_2,
  input  U,
  input  V,
  input  W,
  input  in_27,
  input  X,
  input  Y,
  input  Z,
  output out_31,
  output out_32,
  output out_33,
  output out_34,
  output out_35,
  output out_36,
  output out_37,
  output out_38,
  output out_39,
  output out_40,
  output out_41,
  output out_42,
  output out_43,
  output out_44,
  output out_45,
  output out_46,
  output out_47,
  output out_48,
  output out_49,
  output out_50,
  output out_51,
  output out_52,
  output out_53,
  output out_54,
  output out_55,
  output out_56
);

  wire contatore_2_avanti_di_uno, contatore_3_avanti_di_uno, ONE, rotorea_1_output_1, rotoreb_1_output_1,
       rotorec_1_output_1;
  wire [4:0] contatore_1_posizone_rotore, contatore_2_posizone_rotore, contatore_3_posizone_rotore;
  wire [25:0] riflettore_1_output_26_lettere, rotorea_1_output_26_lettere, rotoreb_1_output_26_lettere,
       rotoreb_1_output_26_lettere_2, rotorec_1_output_26_lettere, rotorec_1_output_26_lettere_2;

  RIFLETTORE riflettore_1 (
    .INPUT_1(rotorec_1_output_1), .INPUT_26_LETTERE(rotorec_1_output_26_lettere),
    .OUTPUT_26_LETTERE(riflettore_1_output_26_lettere));
  ROTOREC rotorec_1 (
    .OUTPUT_1(rotorec_1_output_1), .INPUT_1(rotoreb_1_output_1), .in_3(contatore_1_posizone_rotore),
    .INPUT_26_LETTERE(rotoreb_1_output_26_lettere), .OUTPUT_26_LETTERE(rotorec_1_output_26_lettere),
    .INPUT_26_LETTERE_2(riflettore_1_output_26_lettere), .OUTPUT_26_LETTERE_2(rotorec_1_output_26_lettere_2));
  CONTATORE contatore_1 (
    .WRITE(contatore_2_avanti_di_uno), .POSIZONE_ROTORE(contatore_1_posizone_rotore),
    .POSIZIONE_INIZIALE_ROTORE(in_4), .INIT(in_27));  // open: AVANTI_DI_UNO
  CONTATORE contatore_2 (
    .WRITE(contatore_3_avanti_di_uno), .POSIZONE_ROTORE(contatore_2_posizone_rotore),
    .AVANTI_DI_UNO(contatore_2_avanti_di_uno), .POSIZIONE_INIZIALE_ROTORE(in_5), .INIT(in_27));
  ROTOREB rotoreb_1 (
    .OUTPUT_1(rotoreb_1_output_1), .INPUT_1(rotorea_1_output_1),
    .INPUT_26_LETTERE(rotorea_1_output_26_lettere), .OUTPUT_26_LETTERE(rotoreb_1_output_26_lettere),
    .INPUT_26_LETTERE_2(rotorec_1_output_26_lettere_2), .OUTPUT_26_LETTERE_2(rotoreb_1_output_26_lettere_2),
    .POSIZIONE_ROTORE(contatore_2_posizone_rotore));
  CONTATORE contatore_3 (
    .WRITE(ONE), .POSIZONE_ROTORE(contatore_3_posizone_rotore), .AVANTI_DI_UNO(contatore_3_avanti_di_uno),
    .POSIZIONE_INIZIALE_ROTORE(in_6), .INIT(in_27));
  ROTOREA rotorea_1 (
    .POSIZIONE_ROTORE(contatore_3_posizone_rotore), .INPUT_1(ONE), .OUTPUT_1(rotorea_1_output_1),
    .OUTPUT_26_LETTERE(rotorea_1_output_26_lettere),
    .INPUT_26_LETTERE({Z, Y, X, W, V, U, S_2, S, R, Q, P, O, N, M, L, K, J, I, H, G, F, E, D, C, B, A}),
    .INPUT_26_LETTERE_2(rotoreb_1_output_26_lettere_2),
    .OUTPUT_26_LETTERE_2({out_56, out_55, out_54, out_53, out_52, out_51, out_50, out_49, out_48, out_47, out_46, out_45, out_44, out_43, out_42, out_41, out_40, out_39, out_38, out_37, out_36, out_35, out_34, out_33, out_32, out_31}));
  or or_1 (ONE, A, B, C, D, E, F, G, H, I, J, K, L, M, N, O, P, Q, R, S, S_2, U, V, W, X, Y, Z);

  // Other names for the same wires on the sheet: _7 = in_27;
  //   OUT[25:0] = {out_56, out_55, out_54, out_53, out_52, out_51, out_50, out_49, out_48, out_47, out_46, out_45, out_44, out_43, out_42, out_41, out_40, out_39, out_38, out_37, out_36, out_35, out_34, out_33, out_32, out_31}

  // Notes on the sheet:
  //   ENIGMA
endmodule

module CONTATORE (
  input  INIT,
  input  [4:0] POSIZIONE_INIZIALE_ROTORE,
  input  WRITE,
  output [4:0] POSIZONE_ROTORE,
  output AVANTI_DI_UNO
);

  wire and_1_out, and_3_out, comparator_1_gt, multiplexer_1_out, multiplexer_4_out, not_1_out, not_2_out;
  wire [4:0] adder_1_out, latch_d_6_q, multiplexer_2_out, multiplexer_3_out;

  LATCH_D latch_d_1 (.D(multiplexer_3_out[4]), .CLK(multiplexer_1_out), .Q(POSIZONE_ROTORE[4]));
  Multiplexer #(.enable("false")) multiplexer_1 (.in0(WRITE), .in1(INIT), .out(multiplexer_1_out), .sel(INIT));
  LATCH_D latch_d_2 (.D(multiplexer_3_out[3]), .CLK(multiplexer_1_out), .Q(POSIZONE_ROTORE[3]));
  Adder #(.width(5)) adder_1 (.a(POSIZONE_ROTORE), .b(5'b00001), .out(adder_1_out));  // open: cin, cout
  LATCH_D latch_d_3 (.D(multiplexer_3_out[2]), .CLK(multiplexer_1_out), .Q(POSIZONE_ROTORE[2]));
  Comparator #(.width(5), .mode("unsigned")) comparator_1 (
    .a(adder_1_out), .b(5'b11001), .gt(comparator_1_gt));  // open: eq, lt
  LATCH_D latch_d_4 (.D(multiplexer_3_out[1]), .CLK(multiplexer_1_out), .Q(POSIZONE_ROTORE[1]));
  Multiplexer #(.width(5), .enable("false")) multiplexer_2 (
    .in0(adder_1_out), .in1({5{1'b0}}), .out(multiplexer_2_out), .sel(comparator_1_gt));
  LATCH_D latch_d_5 (.D(multiplexer_3_out[0]), .CLK(multiplexer_1_out), .Q(POSIZONE_ROTORE[0]));
  not not_1 (not_1_out, INIT);
  and and_1 (and_1_out, ~multiplexer_3_out[4], ~multiplexer_3_out[3], ~multiplexer_3_out[2], ~multiplexer_3_out[1], ~multiplexer_3_out[0]);  // AND_Gate
  Multiplexer #(.width(5), .enable("false")) multiplexer_3 (
    .in0(POSIZIONE_INIZIALE_ROTORE), .in1(latch_d_6_q), .out(multiplexer_3_out), .sel(not_1_out));
  Multiplexer #(.enable("false")) multiplexer_4 (.in0(and_1_out), .in1(1'b0), .out(multiplexer_4_out), .sel(INIT));
  and and_2 (AVANTI_DI_UNO, multiplexer_4_out, and_3_out);
  LATCH_D latch_d_6 (.D(multiplexer_2_out[0]), .CLK(not_2_out), .Q(latch_d_6_q[0]));
  not not_2 (not_2_out, multiplexer_1_out);
  LATCH_D latch_d_7 (.D(multiplexer_2_out[1]), .CLK(not_2_out), .Q(latch_d_6_q[1]));
  LATCH_D latch_d_8 (.D(multiplexer_2_out[2]), .CLK(not_2_out), .Q(latch_d_6_q[2]));
  LATCH_D latch_d_9 (.D(multiplexer_2_out[3]), .CLK(not_2_out), .Q(latch_d_6_q[3]));
  and and_3 (and_3_out, ~multiplexer_2_out[4], ~multiplexer_2_out[3], ~multiplexer_2_out[2], ~multiplexer_2_out[1], multiplexer_2_out[0]);  // AND_Gate
  LATCH_D latch_d_10 (.D(multiplexer_2_out[4]), .CLK(not_2_out), .Q(latch_d_6_q[4]));
endmodule

module ENIGMA_GUI (
  input  [4:0] in_1,
  input  [4:0] in_2,
  input  [4:0] in_3,
  input  W,
  input  in_5,
  input  in_6,
  input  in_7,
  input  in_8,
  input  in_9,
  input  in_10,
  input  in_11,
  input  in_12,
  input  in_13,
  input  in_14,
  input  in_15,
  input  in_16,
  input  in_17,
  input  in_18,
  input  in_19,
  input  in_20,
  input  in_21,
  input  in_22,
  input  in_23,
  input  in_24,
  input  in_25,
  input  in_26,
  input  in_27,
  input  in_28,
  input  in_29,
  input  in_30,
  output out_31,
  output out_32,
  output out_33,
  output out_34,
  output out_35,
  output out_36,
  output out_37,
  output out_38,
  output out_39,
  output out_40,
  output out_41,
  output out_42,
  output out_43,
  output out_44,
  output out_45,
  output out_46,
  output out_47,
  output out_48,
  output out_49,
  output out_50,
  output out_51,
  output out_52,
  output out_53,
  output out_54,
  output out_55,
  output out_56
);

  colore_marrone colore_marrone_1 ();
  colore_marrone colore_marrone_2 ();
  colore_marrone colore_marrone_3 ();
  colore_marrone colore_marrone_4 ();
  colore_marrone colore_marrone_5 ();
  colore_marrone colore_marrone_6 ();
  colore_marrone colore_marrone_7 ();
  colore_marrone colore_marrone_8 ();
  colore_marrone colore_marrone_9 ();
  colore_marrone colore_marrone_10 ();
  colore_marrone colore_marrone_11 ();
  colore_marrone colore_marrone_12 ();
  colore_marrone colore_marrone_13 ();
  colore_marrone colore_marrone_14 ();
  colore_marrone colore_marrone_15 ();
  colore_marrone colore_marrone_16 ();
  colore_marrone colore_marrone_17 ();
  colore_marrone colore_marrone_18 ();
  colore_marrone colore_marrone_19 ();
  colore_marrone colore_marrone_20 ();
  colore_marrone colore_marrone_21 ();
  colore_marrone colore_marrone_22 ();
  colore_marrone colore_marrone_23 ();
  colore_marrone colore_marrone_24 ();
  colore_marrone colore_marrone_25 ();
  colore_marrone colore_marrone_26 ();
  colore_marrone colore_marrone_27 ();
  colore_marrone colore_marrone_28 ();
  colore_marrone colore_marrone_29 ();
  colore_marrone colore_marrone_30 ();
  colore_marrone colore_marrone_31 ();
  colore_marrone colore_marrone_32 ();
  ENIGMA enigma_1 (
    .out_31(out_41), .out_32(out_54), .out_33(out_52), .out_34(out_43), .out_35(out_33), .out_36(out_44),
    .out_37(out_45), .out_38(out_46), .out_39(out_38), .out_40(out_47), .out_41(out_48), .out_42(out_49),
    .out_43(out_56), .out_44(out_55), .out_45(out_39), .out_46(out_40), .out_47(out_31), .out_48(out_34),
    .out_49(out_42), .out_50(out_35), .out_51(out_37), .out_52(out_53), .out_53(out_32), .in_27(W),
    .out_54(out_51), .out_55(out_36), .out_56(out_50), .A(in_15), .B(in_28), .C(in_26), .D(in_17), .E(in_7),
    .F(in_18), .G(in_19), .H(in_20), .I(in_12), .J(in_21), .K(in_22), .L(in_23), .M(in_30), .N(in_29),
    .O(in_13), .P(in_14), .Q(in_5), .R(in_8), .S(in_16), .S_2(in_9), .U(in_11), .V(in_27), .W(in_6),
    .X(in_25), .Y(in_10), .Z(in_24), .in_4(in_3), .in_5(in_2), .in_6(in_1));
  colore_marrone colore_marrone_33 ();
  colore_marrone colore_marrone_34 ();
  colore_marrone colore_marrone_35 ();
  colore_marrone colore_marrone_36 ();
  colore_marrone colore_marrone_37 ();
  colore_marrone colore_marrone_38 ();
  colore_marrone colore_marrone_39 ();
  colore_marrone colore_marrone_40 ();
  colore_marrone colore_marrone_41 ();
  colore_marrone colore_marrone_42 ();
  colore_marrone colore_marrone_43 ();
  colore_marrone colore_marrone_44 ();
  colore_marrone colore_marrone_45 ();
  colore_marrone colore_marrone_46 ();
  colore_marrone colore_marrone_47 ();
  colore_marrone colore_marrone_48 ();
  colore_marrone colore_marrone_49 ();
  colore_marrone colore_marrone_50 ();
  colore_marrone colore_marrone_51 ();
  colore_marrone colore_marrone_52 ();
  colore_marrone colore_marrone_53 ();
  colore_marrone colore_marrone_54 ();
  colore_marrone colore_marrone_55 ();
  colore_marrone colore_marrone_56 ();
  colore_marrone colore_marrone_57 ();
  colore_marrone colore_marrone_58 ();
  colore_marrone colore_marrone_59 ();
  colore_marrone colore_marrone_60 ();
  colore_marrone colore_marrone_61 ();
  colore_marrone colore_marrone_62 ();
  colore_marrone colore_marrone_63 ();
  colore_marrone colore_marrone_64 ();
  colore_marrone colore_marrone_65 ();
  colore_marrone colore_marrone_66 ();
  colore_marrone colore_marrone_67 ();
  colore_marrone colore_marrone_68 ();
  colore_marrone colore_marrone_69 ();
  colore_marrone colore_marrone_70 ();
  colore_marrone colore_marrone_71 ();
  colore_marrone colore_marrone_72 ();
  colore_marrone colore_marrone_73 ();
  colore_marrone colore_marrone_74 ();
  colore_marrone colore_marrone_75 ();
  colore_marrone colore_marrone_76 ();
  colore_marrone colore_marrone_77 ();
  colore_marrone colore_marrone_78 ();
  colore_marrone colore_marrone_79 ();
  colore_marrone colore_marrone_80 ();
  colore_marrone colore_marrone_81 ();
  colore_marrone colore_marrone_82 ();
  colore_marrone colore_marrone_83 ();
  colore_marrone colore_marrone_84 ();
  colore_marrone colore_marrone_85 ();
  colore_marrone colore_marrone_86 ();
  colore_marrone colore_marrone_87 ();
  colore_marrone colore_marrone_88 ();
  colore_marrone colore_marrone_89 ();
  colore_marrone colore_marrone_90 ();
  colore_marrone colore_marrone_91 ();

  // Other names for the same wires on the sheet: A = out_41; a_t = in_15; B = out_54; b_t = in_28; C = out_52;
  //   c_t = in_26; D = out_43; d_t = in_17; E = out_33; e_t = in_7; F = out_44; f_t = in_18; G = out_45; g_t = in_19;
  //   H = out_46; h_t = in_20; I = out_38; i_t = in_12; J = out_47; j_t = in_21; K = out_48; k_t = in_22; L = out_49;
  //   l_t = in_23; M = out_56; m_t = in_30; N = out_55; n_t = in_29; O = out_39; o_t = in_13; P = out_40; p_t = in_14;
  //   Q = out_31; q_t = in_5; R = out_34; r_t = in_8; S = out_42; s_t = in_16; T = out_35; t_t = in_9; U = out_37;
  //   u_t = in_11; V = out_53; v_t = in_27; W_t = out_32; w_t_t = in_6; X = out_51; x_t = in_25; Y = out_36;
  //   y_t = in_10; Z = out_50; z_t = in_24

  // Notes on the sheet:
  //   ENIGMA
endmodule
