# Fritzing sketch display (saved by Fritzing 0.9.3b)
breadboards: 1

parts:
  Part1 = Arduino Mega 2560 (Rev3)
  LCD1 = LCD screen
  R1 = Resistor [tolerance=±5% resistance=1k package=THT]
  R2 = Resistor [tolerance=±5% resistance=10k package=THT]
  R3 = Resistor [tolerance=±5% resistance=220 package=THT]

nets:
  N1: Part1.D12_PWM, LCD1.RS
  N2: Part1.D11_PWM, LCD1.E
  N3: Part1.D2_PWM, LCD1.DB7
  N4: Part1.D3_PWM, LCD1.DB6
  N5: Part1.D4_PWM, LCD1.DB5
  N6: Part1.D5_PWM, LCD1.DB4
  VSS: LCD1.VSS, LCD1.VDD, LCD1.R/W, LCD1.LED-, R1.Pin_0, R2.Pin_1, R3.Pin_0
  N7: LCD1.V0, R1.Pin_1, R2.Pin_0
  N8: LCD1.LED+, R3.Pin_1
